# Fritzing sketch robot_basic (saved by Fritzing 0.9.4)

parts:
  J4 = female pin header, 5 pins [form="♀ (female)"]
  J5 = female pin header, 5 pins [form="♀ (female)"]
  J6 = female pin header, 2 pins [form="♀ (female)"]
  J7 = female pin header, 2 pins [form="♀ (female)"]  # not connected
  J8 = female pin header, 2 pins [form="♀ (female)"]
  J9 = female pin header, 2 pins [form="♀ (female)"]
  M1 = DC Motor
  M2 = DC Motor
  S1 = Taiway 100-SP-X-T1 SPDT Miniature Toggle Switch [part_number=100-SP-X-T1-0-0-B1-M1 package=THT]
  J3 = female pin header, 2 pins [form="♀ (female)"]
  J10 = female pin header, 2 pins [form="♀ (female)"]
  Part1 = Arduino Uno (Rev3) - ICSP

nets:
  N1: J4.pin1, Part1.GND
  N2: J5.pin1, Part1.VIN
  N3: J6.pin1, S1.L2
  N4: J6.pin2, S1.L1
  N5: J8.pin1, M2.pin_2
  N6: J8.pin2, M2.pin_1
  N7: J9.pin1, M1.pin_2
  N8: J9.pin2, M1.pin_1
  N9: J3.pin1, Part1.D2
  N10: J3.pin2, Part1.D3_PWM
  N11: J10.pin1, Part1.D4
  N12: J10.pin2, Part1.D5_PWM

notes:
  PWR
  MR
  ML
  +
  -
