# Fritzing sketch robot_basic (saved by Fritzing 0.9.4)

parts:
  Part1 = Arduino Uno (Rev3) - ICSP
  M2 = DC Motor
  S1 = Taiway 100-SP-X-T1 SPDT Miniature Toggle Switch [part_number=100-SP-X-T1-0-0-B1-M2 package=THT]
  M1 = DC Motor
  J2 = female pin header, 2 pins [form="♀ (female)"]
  J1 = female pin header, 2 pins [form="♀ (female)"]
  J3 = double row male pin header, 2 pins [form="♂ (male)"]  # not connected
  J4 = double row male pin header, 2 pins [form="♂ (male)"]
  J5 = male pin header, 2 pins [form="♂ (male)"]
  J6 = male pin header, 2 pins [form="♂ (male)"]
  J7 = double row female pin header, 6 pins [form="♀ (female)"]
  J8 = double row female pin header, 6 pins [form="♀ (female)"]

nets:
  N1: Part1.D2, J6.pin2
  N2: Part1.D3_PWM, J6.pin1
  N3: Part1.D4, J5.pin2
  N4: Part1.D5_PWM, J5.pin1
  N5: Part1.GND, J8.pin6
  N6: Part1.VIN, J7.pin6
  N7: M2.pin_1, J2.pin1
  N8: M2.pin_2, J2.pin2
  N9: S1.L1, J4.pin2
  N10: S1.L2, J4.pin1
  N11: M1.pin_1, J1.pin1
  N12: M1.pin_2, J1.pin2

notes:
  - +
  ML
  MR
