# Fritzing sketch ir (saved by Fritzing 0.9.4)

parts:
  Part1 = Arduino Uno (Rev3) - ICSP
  Center = Infrared Proximity Sensor
  Left = Infrared Proximity Sensor
  Right = Infrared Proximity Sensor

nets:
  N1: Part1.A0, Right.Vout
  N2: Part1.A1, Center.Vout
  N3: Part1.A2, Left.Vout
  5V: Part1.5V, Center.Vcc
  GND: Part1.GND, Center.GND
