# Fritzing sketch nunchuck_rcv (saved by Fritzing 0.9.3b)

parts:
  Part1 = Arduino Uno (Rev3) - ICSP
  Part2 = NRF24L01+ Breakout Board

nets:
  N1: Part1.ICSP_MISO, Part1.D12/MISO, Part2.MISO
  N2: Part1.D8, Part2.CS
  N3: Part1.D11_PWM/MOSI, Part2.MOSI
  N4: Part1.D13/SCK, Part2.SCK
  N5: Part1.D7, Part2.CE
  3V3: Part1.3V3, Part2.VCC
  GND: Part1.GND, Part2.GND
