# Fritzing sketch nunchuck_tx (saved by Fritzing 0.9.3b)

parts:
  Part1 = Arduino Uno (Rev3) - ICSP
  Part2 = NRF24L01+ Breakout Board
  J1 = Camdenboss CTB0158-4 [part_number=CTB0158-4 package=THT]

nets:
  N1: Part1.A4/SDA, J1.pin2
  N2: Part1.A5/SCL, J1.pin1
  N3: Part1.ICSP_MISO, Part1.D12/MISO, Part2.MISO
  N4: Part1.D8, Part2.CS
  N5: Part1.D11_PWM/MOSI, Part2.MOSI
  N6: Part1.D13/SCK, Part2.SCK
  N7: Part1.D7, Part2.CE
  3V3: Part1.3V3, Part2.VCC, J1.pin3
  GND: Part1.GND, Part2.GND, J1.pin4

notes:
  -
  +
  d
  c
  Wii Nunchuck
