# Fritzing sketch robot (saved by Fritzing 0.9.3b)

parts:
  Part1 = Arduino Uno (Rev3) - ICSP
  Part2 = NRF24L01+ Breakout Board
  J2 = double row female pin header, 2 pins [form="♀ (female)"]
  J3 = female pin header, 2 pins [form="♀ (female)"]
  J4 = female pin header, 5 pins [form="♀ (female)"]
  J5 = female pin header, 5 pins [form="♀ (female)"]

nets:
  N1: Part1.ICSP_MISO, Part1.D12/MISO, Part2.MISO
  N2: Part1.D8, Part2.CS
  N3: Part1.D9_PWM, J2.pin1
  N4: Part1.D10_PWM/SS, J3.pin1
  N5: Part1.D11_PWM/MOSI, Part2.MOSI
  N6: Part1.D13/SCK, Part2.SCK
  N7: Part1.D4, J2.pin2
  N8: Part1.D6_PWM, J3.pin2
  N9: Part1.D7, Part2.CE
  3V3: Part1.3V3, Part2.VCC
  GND: Part1.GND, Part2.GND, J4.pin1
  N10: Part1.VIN, J5.pin1

notes:
  GND
  BAT
  APS
  BPS
