# Fritzing sketch robot_basic (saved by Fritzing 0.9.3b)

parts:
  Part1 = Arduino Uno (Rev3) - ICSP
  J4 = female pin header, 5 pins [form="♀ (female)"]
  J5 = female pin header, 5 pins [form="♀ (female)"]
  J6 = female pin header, 2 pins [form="♀ (female)"]
  J7 = female pin header, 2 pins [form="♀ (female)"]  # not connected
  J8 = female pin header, 2 pins [form="♀ (female)"]
  J9 = female pin header, 2 pins [form="♀ (female)"]
  M1 = DC Motor
  M2 = DC Motor
  S1 = Taiway 100-SP-X-T1 SPDT Miniature Toggle Switch [part_number=100-SP-X-T1-0-0-B1-M1 package=THT]
  J3 = female pin header, 2 pins [form="♀ (female)"]
  J10 = female pin header, 2 pins [form="♀ (female)"]

nets:
  N1: Part1.D9_PWM, J3.pin1
  N2: Part1.D10_PWM/SS, J3.pin2
  N3: Part1.D4, J10.pin1
  N4: Part1.D6_PWM, J10.pin2
  N5: Part1.GND, J4.pin1
  N6: Part1.VIN, J5.pin1
  N7: J6.pin1, S1.L2
  N8: J6.pin2, S1.L1
  N9: J8.pin1, M2.pin_2
  N10: J8.pin2, M2.pin_1
  N11: J9.pin1, M1.pin_2
  N12: J9.pin2, M1.pin_1

notes:
  PWR
  MR
  ML
  +
  -
