# Fritzing sketch line (saved by Fritzing 0.9.3b)
breadboards: 1

parts:
  Part1 = Arduino Uno (Rev3) - ICSP
  Part2 = Max Power IR LED Kit
  Part3 = Max Power IR LED Kit [part_number=QRE1113]
  Part4 = Max Power IR LED Kit [part_number=QRE1113]

nets:
  N1: Part1.A3, Part3.CONTROL
  N2: Part1.A4/SDA, Part2.CONTROL
  N3: Part1.A5/SCL, Part4.CONTROL
  GND: Part1.GND, Part2.GND, Part3.GND
  VCC: Part1.5V, Part2.VCC, Part3.VCC
