# Fritzing sketch ir (saved by Fritzing 0.9.3b)
breadboards: 1

parts:
  Part1 = Arduino Uno (Rev3) - ICSP
  J1 = Infrared Proximity Sensor
  J3 = Infrared Proximity Sensor
  J2 = Infrared Proximity Sensor

nets:
  N1: Part1.A0, J1.Vout
  N2: Part1.A1, J2.Vout
  N3: Part1.A2, J3.Vout
  VCC: Part1.5V, J1.Vcc, J3.Vcc, J2.Vcc
  GND: Part1.GND, J1.GND, J3.GND, J2.GND
