# Fritzing sketch thermoresistor (saved by Fritzing 0.9.3b)
breadboards: 1

parts:
  Part1 = Arduino Uno (Rev3) - ICSP
  R1 = Photocell (LDR) [package=THT]
  R2 = Photocell (LDR) [package=THT]
  R3 = Photocell (LDR) [package=THT]
  R4 = Resistor [tolerance=±5% resistance=220 package="2010 [SMD]"]
  R5 = Resistor [tolerance=±5% resistance=220 package="2010 [SMD]"]
  R6 = Resistor [tolerance=±5% resistance=220 package="2010 [SMD]"]

nets:
  N1: Part1.A3, R2.pin_0, R6.Pin_1
  N2: Part1.A4/SDA, R3.pin_0
  N3: Part1.A5/SCL, R1.pin_0, R4.Pin_1
  N4: Part1.5V, R1.pin_1, R2.pin_1
  N5: Part1.GND, R4.Pin_0, R5.Pin_0, R6.Pin_0
